# Fritzing sketch CO2 sensor on Raspberry Pi (saved by Fritzing 0.9.3b)

parts:
  Raspberry_Pi_1 = Raspberry Pi 3 [part_number=RPI-3-V1.2]
  TD-er1 = MH-Z19 CO2 sensor [part_number=MH-Z19]
  OLED1 = OLED 1.3" 128x64 I2C SSH1106 (GND/VCC)

nets:
  3V3: Raspberry_Pi_1.3v3, OLED1.VCC
  N1: Raspberry_Pi_1.GPIO2, OLED1.SDA
  N2: Raspberry_Pi_1.GPIO3, Raspberry_Pi_1.GPIO4, OLED1.SCL
  GND: Raspberry_Pi_1.GND, Raspberry_Pi_1.GPIO17, TD-er1.GND, TD-er1.AOT, OLED1.GND
  N3: Raspberry_Pi_1.GPIO18, Raspberry_Pi_1.GPIO15, TD-er1.TX, TD-er1.SR
  N4: Raspberry_Pi_1.GPIO14, TD-er1.RX
  5V: Raspberry_Pi_1.5V, TD-er1.Vin

custom parts:
  OLED 1.3" 128x64 I2C SSH1106 (GND/VCC): OLED 1.3" 128x64 I2C SSH1106 Pinout: GND/VCC/SCL/SDA
